# Fritzing sketch TrinketBreadboard (saved by Fritzing 0.9.2b)
breadboards: 1

parts:
  R1 = Resistor [tolerance=±5% resistance=3.3k package=THT]
  R2 = Resistor [tolerance=±5% resistance=4.7k package=THT]
  LED1 = LED - 5mm [color="Red (633nm)" package="5 mm [THT]"]
  R3 = Resistor [tolerance=±5% resistance=100 package=THT]
  TRINKET1 = Trinket 3V

nets:
  N1: R1.Pin_0, R2.Pin_0, TRINKET1.no_name_yet#7
  N2: R2.Pin_1, R3.Pin_1, TRINKET1.no_name_yet#2
  N3: LED1.cathode, R3.Pin_0
  N4: LED1.anode, TRINKET1.no_name_yet#8

custom parts:
  Trinket 3V: Adafruit Trinket 3V
